# Fritzing sketch Fritzing Schematic (saved by Fritzing 0.9.3b)

parts:
  ENC1 = YumoE6B2 [package="DIP (Dual Inline) [THT]"]
  S2 = Round Pushbutton
  TP1 = TP4056 [chip_label=TP4056 package="DIP (Dual Inline) [THT]"]
  Part1 = Arduino Pro Mini 328 - 3.3 V/8MHz
  Part2 = Lithium Ion Polymer Battery 3.7v 500mAh [part_number=1578]
  S4 = Toggle Switch spst [package=THT]
  Part3 = SPI OLED Monochrome 128x64 0.96 inch

nets:
  N1: ENC1.V, ENC1.A, Part1.D6_PWM, S4.COM
  N2: ENC1.B, Part1.D2
  N3: ENC1.Z, ENC1.GND, TP1.pin6
  N4: S2.leg0, Part1.D3_PWM
  N5: S2.leg1, Part1.GND
  N6: TP1.pin3, S4.L1
  N7: TP1.pin4, Part2.positive
  N8: TP1.pin5, Part2.negative
  N9: Part1.D13/SCK, Part3.SCK
  N10: Part1.D12/MISO, Part3.SDA
  N11: Part1.D10_PWM/SS, Part3.CS
  N12: Part1.D9_PWM, Part3.DC
  N13: Part1.D8, Part3.RES

custom parts:
  TP4056: A DIP stand-in part for whatever IC you want. With 6 pins on a 300mil dual inline package (DIP) footprint.
  Arduino Pro Mini 328 - 3.3 V/8MHz: Versión de Arduino Pro Mini basada en MEGA328P a 8MHz y alimentada a 3.3 voltios.
  Lithium Ion Polymer Battery 3.7v 500mAh: Lithium ion polymer (also known as 'lipo' or 'lipoly') batteries are thin, light and powerful. The output ranges from 4.2V when completely charged to 3.7V. This battery has a capacity of 500mAh for a total of about 1.9 Wh. The batteries come pre-attached with a genuine 2-pin JST-PH connector as shown and include the necessary protection circuitry.
  Toggle Switch spst: Toggle Switch single pole single throw
  SPI OLED Monochrome 128x64 0.96 inch: Unknown 128x64 0.96 inch 128x64 SPI Monochrome OLED display
